# Fritzing sketch enigma (saved by Fritzing 0.9.3b)
breadboards: 1

parts:
  arduino = Arduino Mega 2560 (Rev3)
  R1 = Resistor [tolerance=±5% resistance=10k package=THT]
  R2 = Resistor [tolerance=±5% resistance=10k package=THT]
  R3 = Resistor [tolerance=±5% resistance=10k package=THT]
  R4 = Resistor [tolerance=±5% resistance=10k package=THT]
  R5 = Resistor [tolerance=±5% resistance=10k package=THT]
  R6 = Resistor [tolerance=±5% resistance=10k package=THT]
  R7 = Resistor [tolerance=±5% resistance=10k package=THT]
  R8 = Resistor [tolerance=±5% resistance=10k package=THT]
  R9 = Resistor [tolerance=±5% resistance=10k package=THT]
  R10 = Resistor [tolerance=±5% resistance=10k package=THT]
  R11 = Resistor [tolerance=±5% resistance=10k package=THT]
  R12 = Resistor [tolerance=±5% resistance=10k package=THT]
  R13 = Resistor [tolerance=±5% resistance=10k package=THT]
  R14 = Resistor [tolerance=±5% resistance=10k package=THT]
  R15 = Resistor [tolerance=±5% resistance=10k package=THT]
  R16 = Resistor [tolerance=±5% resistance=10k package=THT]
  R17 = Resistor [tolerance=±5% resistance=10k package=THT]
  R18 = Resistor [tolerance=±5% resistance=10k package=THT]
  R19 = Resistor [tolerance=±5% resistance=10k package=THT]
  R20 = Resistor [tolerance=±5% resistance=10k package=THT]
  R21 = Resistor [tolerance=±5% resistance=10k package=THT]
  R22 = Resistor [tolerance=±5% resistance=10k package=THT]
  R23 = Resistor [tolerance=±5% resistance=10k package=THT]
  R24 = Resistor [tolerance=±5% resistance=10k package=THT]
  R25 = Resistor [tolerance=±5% resistance=10k package=THT]
  R26 = Resistor [tolerance=±5% resistance=10k package=THT]
  J1 = female pin header, 1 pin [form="♀ (female)"]
  J2 = female pin header, 1 pin [form="♀ (female)"]
  J3 = female pin header, 1 pin [form="♀ (female)"]
  J4 = female pin header, 1 pin [form="♀ (female)"]
  J5 = female pin header, 1 pin [form="♀ (female)"]
  J6 = female pin header, 1 pin [form="♀ (female)"]
  J7 = female pin header, 1 pin [form="♀ (female)"]
  J8 = female pin header, 1 pin [form="♀ (female)"]
  J9 = female pin header, 1 pin [form="♀ (female)"]
  J10 = female pin header, 1 pin [form="♀ (female)"]
  J11 = female pin header, 1 pin [form="♀ (female)"]
  J12 = female pin header, 1 pin [form="♀ (female)"]
  J13 = female pin header, 1 pin [form="♀ (female)"]
  J14 = female pin header, 1 pin [form="♀ (female)"]
  J15 = female pin header, 1 pin [form="♀ (female)"]
  J16 = female pin header, 1 pin [form="♀ (female)"]
  J17 = female pin header, 1 pin [form="♀ (female)"]
  J18 = female pin header, 1 pin [form="♀ (female)"]
  J19 = female pin header, 1 pin [form="♀ (female)"]
  J20 = female pin header, 1 pin [form="♀ (female)"]
  J21 = female pin header, 1 pin [form="♀ (female)"]
  J22 = female pin header, 1 pin [form="♀ (female)"]
  J23 = female pin header, 1 pin [form="♀ (female)"]
  J24 = female pin header, 1 pin [form="♀ (female)"]
  J25 = female pin header, 1 pin [form="♀ (female)"]
  J26 = female pin header, 1 pin [form="♀ (female)"]
  D1 = Rectifier Diode [part_number=1N4001 package="300 mil [THT]"]
  D2 = Rectifier Diode [part_number=1N4001 package="300 mil [THT]"]
  D3 = Rectifier Diode [part_number=1N4001 package="300 mil [THT]"]
  D4 = Rectifier Diode [part_number=1N4001 package="300 mil [THT]"]
  D5 = Rectifier Diode [part_number=1N4001 package="300 mil [THT]"]
  D6 = Rectifier Diode [part_number=1N4001 package="300 mil [THT]"]
  D7 = Rectifier Diode [part_number=1N4001 package="300 mil [THT]"]
  D8 = Rectifier Diode [part_number=1N4001 package="300 mil [THT]"]
  D9 = Rectifier Diode [part_number=1N4001 package="300 mil [THT]"]
  D10 = Rectifier Diode [part_number=1N4001 package="300 mil [THT]"]
  D11 = Rectifier Diode [part_number=1N4001 package="300 mil [THT]"]
  D12 = Rectifier Diode [part_number=1N4001 package="300 mil [THT]"]
  D13 = Rectifier Diode [part_number=1N4001 package="300 mil [THT]"]
  D14 = Rectifier Diode [part_number=1N4001 package="300 mil [THT]"]
  D15 = Rectifier Diode [part_number=1N4001 package="300 mil [THT]"]
  D16 = Rectifier Diode [part_number=1N4001 package="300 mil [THT]"]
  D17 = Rectifier Diode [part_number=1N4001 package="300 mil [THT]"]
  D18 = Rectifier Diode [part_number=1N4001 package="300 mil [THT]"]
  D19 = Rectifier Diode [part_number=1N4001 package="300 mil [THT]"]
  D20 = Rectifier Diode [part_number=1N4001 package="300 mil [THT]"]
  D21 = Rectifier Diode [part_number=1N4001 package="300 mil [THT]"]
  D22 = Rectifier Diode [part_number=1N4001 package="300 mil [THT]"]
  D23 = Rectifier Diode [part_number=1N4001 package="300 mil [THT]"]
  D24 = Rectifier Diode [part_number=1N4001 package="300 mil [THT]"]
  D25 = Rectifier Diode [part_number=1N4001 package="300 mil [THT]"]
  D26 = Rectifier Diode [part_number=1N4001 package="300 mil [THT]"]

nets:
  N1: arduino.D13_PWM, R23.Pin_0, J1.pin1
  N2: arduino.D12_PWM, R22.Pin_0, J11.pin1
  N3: arduino.D11_PWM, R20.Pin_0, J12.pin1
  N4: arduino.D10_PWM, R21.Pin_0, J13.pin1
  N5: arduino.D9_PWM, R5.Pin_0, J14.pin1
  N6: arduino.D8_PWM, R14.Pin_0, J19.pin1
  N7: arduino.D2_PWM, R11.Pin_0, J21.pin1
  N8: arduino.D3_PWM, R2.Pin_0, J4.pin1
  N9: arduino.D4_PWM, R12.Pin_0, J3.pin1
  N10: arduino.D5_PWM, R3.Pin_0, J2.pin1
  N11: arduino.D6_PWM, R13.Pin_0, J20.pin1
  N12: arduino.D7_PWM, R4.Pin_0, J15.pin1
  N13: arduino.D22, R6.Pin_0, J5.pin1
  N14: arduino.D23, R26.Pin_0, J6.pin1
  N15: arduino.D24, R25.Pin_0, J7.pin1
  N16: arduino.D25, R16.Pin_0, J8.pin1
  N17: arduino.D26, R15.Pin_0, J9.pin1
  N18: arduino.D27, R8.Pin_0, J10.pin1
  N19: arduino.D28, R7.Pin_0, J22.pin1
  N20: arduino.D29, R17.Pin_0, J23.pin1
  N21: arduino.D30, R9.Pin_0, J24.pin1
  N22: arduino.D31, R18.Pin_0, J25.pin1
  N23: arduino.D32, R10.Pin_0, J26.pin1
  N24: arduino.D33, R19.Pin_0, J16.pin1
  N25: arduino.D34, R1.Pin_0, J17.pin1
  N26: arduino.D35, R24.Pin_0, J18.pin1
  N27: R1.Pin_1, D25.anode
  N28: R2.Pin_1, D11.anode
  N29: R3.Pin_1, D10.anode
  N30: R4.Pin_1, D5.anode
  N31: R5.Pin_1, D6.anode
  N32: R6.Pin_1, D13.anode
  N33: R7.Pin_1, D20.anode
  N34: R8.Pin_1, D16.anode
  N35: R9.Pin_1, D19.anode
  N36: R10.Pin_1, D24.anode
  N37: R11.Pin_1, D9.anode
  N38: R12.Pin_1, D12.anode
  N39: R13.Pin_1, D7.anode
  N40: R14.Pin_1, D8.anode
  N41: R15.Pin_1, D18.anode
  N42: R16.Pin_1, D17.anode
  N43: R17.Pin_1, D21.anode
  N44: R18.Pin_1, D23.anode
  N45: R19.Pin_1, D22.anode
  N46: R20.Pin_1, D4.anode
  N47: R21.Pin_1, D3.anode
  N48: R22.Pin_1, D2.anode
  N49: R23.Pin_1, D1.anode
  N50: R24.Pin_1, D26.anode
  N51: R25.Pin_1, D15.anode
  N52: R26.Pin_1, D14.anode
  GND: D1.cathode, D2.cathode, D3.cathode, D4.cathode, D5.cathode, D6.cathode, D7.cathode, D8.cathode, D9.cathode, D10.cathode, D11.cathode, D12.cathode, D13.cathode, D14.cathode, D15.cathode, D16.cathode, D17.cathode, D18.cathode, D19.cathode, D20.cathode, D21.cathode, D22.cathode, D23.cathode, D24.cathode, D25.cathode, D26.cathode
